// Logisim project Relógio.circ as structural Verilog: 6 circuits, main circuit main
module main (
  input  in_1,
  input  in_2,
  input  in_3,
  input  in_4,
  input  in_5
);

  wire and_1_out, clock_de_0_a_5_1_vai_1, clock_de_0_a_5_2_vai_1, clock_de_0_a_9_1_vai_1,
       clock_de_0_a_9_2_vai_1, clock_inicial_1_vai_1, display_1_out_2, display_1_out_3, display_1_out_4,
       display_1_out_5, display_1_out_6, display_1_out_7, display_1_out_8, display_2_out_2, display_2_out_3,
       display_2_out_4, display_2_out_5, display_2_out_6, display_2_out_7, display_2_out_8, display_3_out_2,
       display_3_out_3, display_3_out_4, display_3_out_5, display_3_out_6, display_3_out_7, display_3_out_8,
       display_4_out_2, display_4_out_3, display_4_out_4, display_4_out_5, display_4_out_6, display_4_out_7,
       display_4_out_8, display_5_out_2, display_5_out_3, display_5_out_4, display_5_out_5, display_5_out_6,
       display_5_out_7, display_5_out_8, display_6_out_2, display_6_out_3, display_6_out_4, display_6_out_5,
       display_6_out_6, display_6_out_7, display_6_out_8, multiplexer_1_out;
  wire [3:0] clock_de_0_a_5_1_a, clock_de_0_a_5_2_a, clock_de_0_a_9_1_a, clock_de_0_a_9_2_a,
       clock_de_hora_1_a, clock_inicial_1_a;

  clock_de_hora clock_de_hora_1 (
    .clock(clock_de_0_a_9_1_vai_1), .reset(multiplexer_1_out), .A(clock_de_hora_1_a[0]),
    .B(clock_de_hora_1_a[1]), .C(clock_de_hora_1_a[2]), .D(clock_de_hora_1_a[3]));  // open: vai_1
  Display display_1 (
    .in_1(clock_de_hora_1_a), .out_2(display_1_out_2), .out_3(display_1_out_3), .out_4(display_1_out_4),
    .out_5(display_1_out_5), .out_6(display_1_out_6), .out_7(display_1_out_7), .out_8(display_1_out_8));
  _7_Segment_Display u_7_segment_display_1 (
    .g(display_1_out_5), .f(display_1_out_4), .a(display_1_out_3), .b(display_1_out_2), .e(display_1_out_6),
    .d(display_1_out_7), .c(display_1_out_8));  // open: dp
  clock_de_0_a_9 clock_de_0_a_9_1 (
    .clock(clock_de_0_a_5_1_vai_1), .reset(multiplexer_1_out), .A(clock_de_0_a_9_1_a[0]),
    .B(clock_de_0_a_9_1_a[1]), .C(clock_de_0_a_9_1_a[2]), .D(clock_de_0_a_9_1_a[3]),
    .vai_1(clock_de_0_a_9_1_vai_1));
  _7_Segment_Display u_7_segment_display_2 (
    .g(display_2_out_5), .f(display_2_out_4), .a(display_2_out_3), .b(display_2_out_2), .e(display_2_out_6),
    .d(display_2_out_7), .c(display_2_out_8));  // open: dp
  and and_1 (and_1_out, ~display_1_out_8, display_1_out_7, display_1_out_6, display_1_out_5, ~display_1_out_4, display_1_out_3, display_1_out_2, display_2_out_8, ~display_2_out_7, ~display_2_out_6, display_2_out_5, display_2_out_4, ~display_2_out_3, display_2_out_2);  // AND_Gate
  Display display_2 (
    .in_1(clock_de_0_a_9_1_a), .out_2(display_2_out_2), .out_3(display_2_out_3), .out_4(display_2_out_4),
    .out_5(display_2_out_5), .out_6(display_2_out_6), .out_7(display_2_out_7), .out_8(display_2_out_8));
  clock_de_0_a_5 clock_de_0_a_5_1 (
    .clock(clock_de_0_a_9_2_vai_1), .reset(in_1), .A(clock_de_0_a_5_1_a[0]), .B(clock_de_0_a_5_1_a[1]),
    .C(clock_de_0_a_5_1_a[2]), .D(clock_de_0_a_5_1_a[3]), .vai_1(clock_de_0_a_5_1_vai_1));
  Display display_3 (
    .in_1(clock_de_0_a_5_1_a), .out_2(display_3_out_2), .out_3(display_3_out_3), .out_4(display_3_out_4),
    .out_5(display_3_out_5), .out_6(display_3_out_6), .out_7(display_3_out_7), .out_8(display_3_out_8));
  _7_Segment_Display u_7_segment_display_3 (
    .g(display_3_out_5), .f(display_3_out_4), .a(display_3_out_3), .b(display_3_out_2), .e(display_3_out_6),
    .d(display_3_out_7), .c(display_3_out_8));  // open: dp
  clock_de_0_a_9 clock_de_0_a_9_2 (
    .clock(clock_de_0_a_5_2_vai_1), .reset(in_2), .A(clock_de_0_a_9_2_a[0]), .B(clock_de_0_a_9_2_a[1]),
    .C(clock_de_0_a_9_2_a[2]), .D(clock_de_0_a_9_2_a[3]), .vai_1(clock_de_0_a_9_2_vai_1));
  Multiplexer #(.enable("false")) multiplexer_1 (.in0(in_5), .in1(and_1_out), .out(multiplexer_1_out), .sel(and_1_out));
  _7_Segment_Display u_7_segment_display_4 (
    .g(display_4_out_5), .f(display_4_out_4), .a(display_4_out_3), .b(display_4_out_2), .e(display_4_out_6),
    .d(display_4_out_7), .c(display_4_out_8));  // open: dp
  Display display_4 (
    .in_1(clock_de_0_a_9_2_a), .out_2(display_4_out_2), .out_3(display_4_out_3), .out_4(display_4_out_4),
    .out_5(display_4_out_5), .out_6(display_4_out_6), .out_7(display_4_out_7), .out_8(display_4_out_8));
  clock_de_0_a_5 clock_de_0_a_5_2 (
    .clock(clock_inicial_1_vai_1), .reset(in_3), .A(clock_de_0_a_5_2_a[0]), .B(clock_de_0_a_5_2_a[1]),
    .C(clock_de_0_a_5_2_a[2]), .D(clock_de_0_a_5_2_a[3]), .vai_1(clock_de_0_a_5_2_vai_1));
  _7_Segment_Display u_7_segment_display_5 (
    .g(display_5_out_5), .f(display_5_out_4), .a(display_5_out_3), .b(display_5_out_2), .e(display_5_out_6),
    .d(display_5_out_7), .c(display_5_out_8));  // open: dp
  Display display_5 (
    .in_1(clock_de_0_a_5_2_a), .out_2(display_5_out_2), .out_3(display_5_out_3), .out_4(display_5_out_4),
    .out_5(display_5_out_5), .out_6(display_5_out_6), .out_7(display_5_out_7), .out_8(display_5_out_8));
  Clock_inicial clock_inicial_1 (
    .reset(in_4), .A(clock_inicial_1_a[0]), .B(clock_inicial_1_a[1]), .C(clock_inicial_1_a[2]),
    .D(clock_inicial_1_a[3]), .vai_1(clock_inicial_1_vai_1));
  _7_Segment_Display u_7_segment_display_6 (
    .g(display_6_out_5), .f(display_6_out_4), .a(display_6_out_3), .b(display_6_out_2), .e(display_6_out_6),
    .d(display_6_out_7), .c(display_6_out_8));  // open: dp
  Display display_6 (
    .in_1(clock_inicial_1_a), .out_2(display_6_out_2), .out_3(display_6_out_3), .out_4(display_6_out_4),
    .out_5(display_6_out_5), .out_6(display_6_out_6), .out_7(display_6_out_7), .out_8(display_6_out_8));
endmodule

module Clock_inicial (
  input  reset,
  output A,
  output B,
  output C,
  output D,
  output vai_1
);

  wire and_1_out, clock_1_out, d_ff_1_q, d_ff_2_q, d_ff_3_q, d_ff_4_q;

  Clock clock_1 (.out(clock_1_out));
  and and_1 (and_1_out, ~A, B, ~C, D);  // AND_Gate
  D_Flip_Flop d_ff_1 (.clk(clock_1_out), .D(A), .Q(d_ff_1_q), .preset(vai_1));  // open: Qn, en, reset
  D_Flip_Flop d_ff_2 (.clk(d_ff_1_q), .D(B), .Q(d_ff_2_q), .preset(vai_1));  // open: Qn, en, reset
  D_Flip_Flop d_ff_3 (.clk(d_ff_2_q), .D(C), .Q(d_ff_3_q), .preset(vai_1));  // open: Qn, en, reset
  D_Flip_Flop d_ff_4 (.clk(d_ff_3_q), .D(D), .Q(d_ff_4_q), .preset(vai_1));  // open: Qn, en, reset
  Multiplexer multiplexer_1 (.in0(and_1_out), .in1(reset), .out(vai_1), .sel(reset));  // open: en
  not not_1 (A, d_ff_1_q);
  not not_2 (B, d_ff_2_q);
  not not_3 (C, d_ff_3_q);
  not not_4 (D, d_ff_4_q);
endmodule

module clock_de_0_a_9 (
  input  clock,
  input  reset,
  output A,
  output B,
  output C,
  output D,
  output vai_1
);

  wire and_1_out, d_ff_1_q, d_ff_2_q, d_ff_3_q, d_ff_4_q;

  and and_1 (and_1_out, ~A, B, ~C, D);  // AND_Gate
  D_Flip_Flop d_ff_1 (.clk(clock), .D(A), .Q(d_ff_1_q), .preset(vai_1));  // open: Qn, en, reset
  D_Flip_Flop d_ff_2 (.clk(d_ff_1_q), .D(B), .Q(d_ff_2_q), .preset(vai_1));  // open: Qn, en, reset
  D_Flip_Flop d_ff_3 (.clk(d_ff_2_q), .D(C), .Q(d_ff_3_q), .preset(vai_1));  // open: Qn, en, reset
  D_Flip_Flop d_ff_4 (.clk(d_ff_3_q), .D(D), .Q(d_ff_4_q), .preset(vai_1));  // open: Qn, en, reset
  Multiplexer multiplexer_1 (.in0(and_1_out), .in1(reset), .out(vai_1), .sel(reset));  // open: en
  not not_1 (A, d_ff_1_q);
  not not_2 (B, d_ff_2_q);
  not not_3 (C, d_ff_3_q);
  not not_4 (D, d_ff_4_q);
endmodule

module clock_de_0_a_5 (
  input  clock,
  input  reset,
  output A,
  output B,
  output C,
  output D,
  output vai_1
);

  wire and_1_out, d_ff_1_q, d_ff_2_q, d_ff_3_q, d_ff_4_q;

  and and_1 (and_1_out, ~A, B, C, ~D);  // AND_Gate
  D_Flip_Flop d_ff_1 (.clk(clock), .D(A), .Q(d_ff_1_q), .preset(vai_1));  // open: Qn, en, reset
  D_Flip_Flop d_ff_2 (.clk(d_ff_1_q), .D(B), .Q(d_ff_2_q), .preset(vai_1));  // open: Qn, en, reset
  D_Flip_Flop d_ff_3 (.clk(d_ff_2_q), .D(C), .Q(d_ff_3_q), .preset(vai_1));  // open: Qn, en, reset
  D_Flip_Flop d_ff_4 (.clk(d_ff_3_q), .D(D), .Q(d_ff_4_q), .preset(vai_1));  // open: Qn, en, reset
  Multiplexer multiplexer_1 (.in0(and_1_out), .in1(reset), .out(vai_1), .sel(reset));  // open: en
  not not_1 (A, d_ff_1_q);
  not not_2 (B, d_ff_2_q);
  not not_3 (C, d_ff_3_q);
  not not_4 (D, d_ff_4_q);
endmodule

module Display (
  input  [3:0] in_1,
  output out_2,
  output out_3,
  output out_4,
  output out_5,
  output out_6,
  output out_7,
  output out_8
);

  Multiplexer #(.select(4)) multiplexer_1 (
    .in0(1'b1), .in1(1'b0), .in2(1'b1), .in3(1'b1), .in4(1'b0), .in5(1'b1), .in6(1'b1), .in7(1'b1),
    .in8(1'b1), .in9(1'b1), .out(out_3), .sel(in_1));  // open: in10, in11, in12, in13, in14, in15, en
  Multiplexer #(.select(4)) multiplexer_2 (
    .in0(1'b1), .in1(1'b0), .in2(1'b0), .in3(1'b0), .in4(1'b1), .in5(1'b1), .in6(1'b1), .in7(1'b0),
    .in8(1'b1), .in9(1'b1), .out(out_4), .sel(in_1));  // open: in10, in11, in12, in13, in14, in15, en
  Multiplexer #(.select(4)) multiplexer_3 (
    .in0(1'b1), .in1(1'b0), .in2(1'b1), .in3(1'b0), .in4(1'b0), .in5(1'b0), .in6(1'b1), .in7(1'b0),
    .in8(1'b1), .in9(1'b0), .out(out_6), .sel(in_1));  // open: in10, in11, in12, in13, in14, in15, en
  Multiplexer #(.select(4)) multiplexer_4 (
    .in0(1'b1), .in1(1'b1), .in2(1'b1), .in3(1'b1), .in4(1'b1), .in5(1'b0), .in6(1'b0), .in7(1'b1),
    .in8(1'b1), .in9(1'b1), .out(out_2), .sel(in_1));  // open: in10, in11, in12, in13, in14, in15, en
  Multiplexer #(.select(4)) multiplexer_5 (
    .in0(1'b0), .in1(1'b0), .in2(1'b1), .in3(1'b1), .in4(1'b1), .in5(1'b1), .in6(1'b1), .in7(1'b0),
    .in8(1'b1), .in9(1'b1), .out(out_5), .sel(in_1));  // open: in10, in11, in12, in13, in14, in15, en
  Multiplexer #(.select(4)) multiplexer_6 (
    .in0(1'b1), .in1(1'b0), .in2(1'b1), .in3(1'b1), .in4(1'b0), .in5(1'b1), .in6(1'b1), .in7(1'b0),
    .in8(1'b1), .in9(1'b1), .out(out_7), .sel(in_1));  // open: in10, in11, in12, in13, in14, in15, en
  Multiplexer #(.select(4)) multiplexer_7 (
    .in0(1'b1), .in1(1'b1), .in2(1'b0), .in3(1'b1), .in4(1'b1), .in5(1'b1), .in6(1'b1), .in7(1'b1),
    .in8(1'b1), .in9(1'b1), .out(out_8), .sel(in_1));  // open: in10, in11, in12, in13, in14, in15, en
  _7_Segment_Display u_7_segment_display_1 (
    .g(out_5), .f(out_4), .a(out_3), .b(out_2), .e(out_6), .d(out_7), .c(out_8));  // open: dp
endmodule

module clock_de_hora (
  input  clock,
  input  reset,
  output A,
  output B,
  output C,
  output D,
  output vai_1
);

  wire and_1_out, d_ff_1_q, d_ff_2_q, d_ff_3_q, d_ff_4_q;

  and and_1 (and_1_out, ~A, ~B, C, D);  // AND_Gate
  D_Flip_Flop d_ff_1 (.clk(clock), .D(A), .Q(d_ff_1_q), .preset(vai_1));  // open: Qn, en, reset
  D_Flip_Flop d_ff_2 (.clk(d_ff_1_q), .D(B), .Q(d_ff_2_q), .preset(vai_1));  // open: Qn, en, reset
  D_Flip_Flop d_ff_3 (.clk(d_ff_2_q), .D(C), .Q(d_ff_3_q), .preset(vai_1));  // open: Qn, en, reset
  D_Flip_Flop d_ff_4 (.clk(d_ff_3_q), .D(D), .Q(d_ff_4_q), .preset(vai_1));  // open: Qn, en, reset
  Multiplexer multiplexer_1 (.in0(and_1_out), .in1(reset), .out(vai_1), .sel(reset));  // open: en
  not not_1 (A, d_ff_1_q);
  not not_2 (B, d_ff_2_q);
  not not_3 (C, d_ff_3_q);
  not not_4 (D, d_ff_4_q);
endmodule
